# Fritzing sketch soDoNguyenLy (saved by Fritzing 0.9.3b)

parts:
  Raspberry_Pi_4 = Raspberry Pi 4B  # not connected
  ESP32 = ESP32 DevKitc V4
  Driver_1 = L298N DC motor driver
  YDLidar_X3 = YDLIDAR X2
  Driver_2 = L298N DC motor driver
  Left_Front = DC Motor with two-phase hall-encoder [part_number=VT-E-G25A-06-177E]
  Right_Front = DC Motor with two-phase hall-encoder [part_number=VT-E-G25A-06-177E]
  Left_Back = DC Motor with two-phase hall-encoder [part_number=VT-E-G25A-06-177E]
  Right_Back = DC Motor with two-phase hall-encoder [part_number=VT-E-G25A-06-177E]
  Battery1 = Battery  # not connected
  3_3V = terminal block 4position
  GND = terminal block 4position
  Power_Bank_5V = 3-USB-Power-Bank-Battery-Pack
  USBTTL1 = USB TTL Serial Cable
  USBTTL3 = USB A Plug
  USBTTL4 = Micro USB B Plug
  USB-C_5V = Adafruit USB Type C Plug Breakout [part_number=#5978]
  BUCK_3_3V = LM2596 step down module
  SWITCH = Toggle Switch spst [package=THT]
  Buck_12V = XL4015 DC-DC CC CV module (blue)
  Battery2 = Battery  # not connected

nets:
  N1: ESP32.IO17, Right_Front.pin3
  N2: ESP32.IO5, Right_Front.pin4
  N3: ESP32.IO18, Driver_1.IN3
  N4: ESP32.IO19, Driver_1.IN1
  N5: ESP32.IO21, Driver_1.IN2
  N6: ESP32.IO22, Left_Front.pin3
  N7: ESP32.IO23, Left_Front.pin4
  N8: ESP32.IO34, Left_Back.pin3
  N9: ESP32.IO35, Left_Back.pin4
  N10: ESP32.IO32, Driver_2.IN1
  N11: ESP32.IO33, Driver_2.IN2
  N12: ESP32.IO25, Right_Back.pin3
  N13: ESP32.IO26, Right_Back.pin4
  N14: ESP32.IO27, Driver_2.IN3
  N15: ESP32.IO14, Driver_2.IN4
  N16: ESP32.IO13, Driver_1.IN4
  N17: Driver_1.OUT1, Left_Front.pin6
  N18: Driver_1.OUT2, Left_Front.pin1
  12V: Driver_1.12V, Driver_2.12V, Buck_12V.pin_3
  GND: Driver_1.GND, Driver_2.GND, Buck_12V.pin_4
  N19: Driver_1.OUT3, Right_Front.pin6
  N20: Driver_1.OUT4, Right_Front.pin1
  N21: YDLidar_X3.Pin_1, USBTTL1.TX
  N22: YDLidar_X3.Pin_2, USBTTL1.RX
  N23: YDLidar_X3.Pin_3, USBTTL1.GND
  N24: YDLidar_X3.Pin_4, USBTTL1.5V
  N25: Driver_2.OUT1, Right_Back.pin6
  N26: Driver_2.OUT2, Right_Back.pin1
  N27: Driver_2.OUT3, Left_Back.pin6
  N28: Driver_2.OUT4, Left_Back.pin1
  N29: Left_Front.pin2, Right_Front.pin2, Left_Back.pin2, Right_Back.pin2, GND.Pin_1, GND.Pin_2, GND.Pin_3, GND.Pin_4, GND.Pin_5, GND.Pin_6, GND.Pin_7, GND.Pin_8, BUCK_3_3V.IN-, BUCK_3_3V.OUT-, Buck_12V.pin_2
  N30: Left_Front.pin5, Right_Front.pin5, Left_Back.pin5, Right_Back.pin5, 3_3V.Pin_1, 3_3V.Pin_2, 3_3V.Pin_3, 3_3V.Pin_4, 3_3V.Pin_5, 3_3V.Pin_6, 3_3V.Pin_7, 3_3V.Pin_8, BUCK_3_3V.OUT+
  N31: Power_Bank_5V.5V+, USB-C_5V.VBUS
  N32: Power_Bank_5V.D+, USB-C_5V.D+
  N33: Power_Bank_5V.D-, USB-C_5V.D-
  GND_2: Power_Bank_5V.GND, USB-C_5V.GND
  N34: USBTTL3.usb, USBTTL4.usb
  N35: BUCK_3_3V.IN+, SWITCH.L1, Buck_12V.pin_1

custom parts:
  ESP32 DevKitc V4: ESP32-DevKitC board with ESP32-WROOM-32 module. ESP32-DevKitC V4 is a small-sized ESP32-based development board produced by Espressif. Most of the pins on the ESP module are broken out to the pin headers on the board. The pins D0, D1, D2, D3, CMD and CLK are used internally for communication between ESP32 and SPI flash memory. They are grouped on both sides near the USB connector. Avoid using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
  L298N DC motor driver: 2x DC motor driver with 78M05 positive voltage regulator (7..35 V) L298N: max 46 V, 2 A Set 5 V Enable jumper to enable 5 V regultor (needed for the L298N) and +5 V output at screw terminal or supply external +5 V at screw terminal Set ENA and/or ENB to +5 V to enable motor permanently or supply ENA and/or ENB with PWM signal IN1 and IN2 set rotation directory for motor A (OUT1/OUT2) IN2 and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
  YDLIDAR X2: The YDLIDAR X2 Lidar is a 360-degree two-dimensional distance measurement product.
  Battery: Your standard 3x 18650 battery pack (11.1 Volts)
  3-USB-Power-Bank-Battery-Pack: INIU B61 Power Bank 10000mAh, 3-Port Design.
  USB A Plug: USB A Plug breadboard only for documetnation purposes.
  Adafruit USB Type C Plug Breakout: Throw out all those Mini and Micro B USB cables you have in a plastic bin - the next generation of USB connectors is here with USB C! You've seen these connectors pop up on all sorts of devices, as the industry moves from micro B or lightning to the new standard. Well, at least until the next standard comes out USB C features a symmetric/reversible connector, more data pins and higher current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
  LM2596 step down module: LM2596 DC-DC step down power supply module 3 A.
  Toggle Switch spst: Toggle Switch single pole single throw
  XL4015 DC-DC CC CV module (blue): XL4015 DC-DC CC/CV module blue
